# Fritzing sketch ESP_18B20 (saved by Fritzing 0.9.0b)
breadboards: 1

parts:
  Part1 = ESPresso LIte V2.0
  R1 = Photocell (LDR) [package=THT]
  R3 = Resistor [tolerance=±5% resistance=1k package="0805 [SMD]"]

nets:
  N1: Part1.no_name_yet#connector_GND1, R1.pin_1
  N2: Part1.no_name_yet#connector_V3, R3.Pin_0
  N3: R1.pin_0, R3.Pin_1
