# Fritzing sketch ESP_DHT11 (saved by Fritzing 0.9.0b)

parts:
  Part1 = ESPresso LIte V2.0
  DHT1 = DHT11 Humitidy and Temperature Sensor

nets:
  N1: Part1.no_name_yet#connector_GND5, DHT1.GND
  N2: Part1.no_name_yet#connector_I121, DHT1.DATA
  N3: Part1.no_name_yet#connector_V33, DHT1.VDD

custom parts:
  DHT11 Humitidy and Temperature Sensor: DHT11 Humidity and Temperature Sensor
