# Fritzing sketch ESP_LCD_i2c (saved by Fritzing 0.9.0b)

parts:
  Part1 = ESPresso LIte V2.0
  LCM1602_IIC1 = LCM1602 IIC [part_number="LCM1602 IIC" chip_label="LCM1602 IIC" package="DIP (Dual Inline) [THT]"]
  U1 = LCD-16X2 [package=lcd-16x2_noholes]

nets:
  N1: Part1.no_name_yet#connector_GND4, LCM1602_IIC1.GND
  N2: Part1.no_name_yet#connector_SCL0, LCM1602_IIC1.SCL
  N3: Part1.no_name_yet#connector_SDA0, LCM1602_IIC1.SDA
  N4: Part1.no_name_yet#connector_V32, LCM1602_IIC1.VCC
  VSS: LCM1602_IIC1.VSS, U1.VSS
  VDD: LCM1602_IIC1.VDD, U1.VDD
  N5: LCM1602_IIC1.V0, U1.VO
  N6: LCM1602_IIC1.RS, U1.RS
  N7: LCM1602_IIC1.RW, U1.R_W
  N8: LCM1602_IIC1.E, U1.E
  N9: LCM1602_IIC1.D0, U1.DB0
  N10: LCM1602_IIC1.D1, U1.DB1
  N11: LCM1602_IIC1.D2, U1.DB2
  N12: LCM1602_IIC1.D3, U1.DB3
  N13: LCM1602_IIC1.D4, U1.DB4
  N14: LCM1602_IIC1.D5, U1.DB5
  N15: LCM1602_IIC1.D6, U1.DB6
  N16: LCM1602_IIC1.D7, U1.DB7
  N17: LCM1602_IIC1.A, U1.A
  N18: LCM1602_IIC1.K, U1.K
  N19: LCM1602_IIC1.LED_A, LCM1602_IIC1.LED_B

custom parts:
  LCM1602 IIC: I2C-Module to use a 1602 or 2004 LCD on with the wire.h libory Serial LCD Modul
