# Fritzing sketch ESP_PIR (saved by Fritzing 0.9.0b)

parts:
  Part1 = ESPresso LIte V2.0
  PIR1 = PIR sensor

nets:
  N1: Part1.no_name_yet#connector_GND0, PIR1.GND
  N2: Part1.no_name_yet#connector_I13, PIR1.SIG
  N3: Part1.no_name_yet#connector_V3, PIR1.VDD
