# Fritzing sketch Sketch_Soil (saved by Fritzing 0.9.0b)

parts:
  Part1 = ESPresso LIte V2.0
  J1 = female pin header, 4 pins [form="♀ (female)"]

nets:
  N1: Part1.no_name_yet#connector_A0, J1.pin2
  N2: Part1.no_name_yet#connector_GND1, J1.pin3
  N3: Part1.no_name_yet#connector_V3, J1.pin4
