# Fritzing sketch Untitled Sketch (saved by Fritzing 0.9.3b)
breadboards: 1

parts:
  Part1 = ESPresso LIte V2.0
  DHT1 = DHT11 Humitidy and Temperature Sensor  # not connected

nets:
  N1: Part1.no_name_yet#connector_CTS0, Part1.no_name_yet#connector_GND3, Part1.no_name_yet#connector_VIN1
  N2: Part1.no_name_yet#connector_DTR0, Part1.no_name_yet#connector_GND1, Part1.no_name_yet#connector_TX0

notes:
  สามารถใช้DHT22ได้ ตำแหน่งขาตรงกัน แก้โค้ดบรรทัดที่4ใน_publish.h จาก #define DHTTYPE DHT11 เป็น #define DHTTYPE DHT22

custom parts:
  DHT11 Humitidy and Temperature Sensor: DHT11 Humidity and Temperature Sensor
