# Fritzing sketch Untitled Sketch (saved by Fritzing 0.9.3b)
breadboards: 1

parts:
  Part1 = ESPresso LIte V2.0
  R1 = Photocell (LDR) [package=THT]
  R2 = Resistor [tolerance=±5% resistance=1k package="1206 [SMD]"]

nets:
  N1: Part1.no_name_yet#connector_A0, R1.pin_1, R2.Pin_0
  N2: Part1.no_name_yet#connector_CTS0, Part1.no_name_yet#connector_GND3, Part1.no_name_yet#connector_VIN1
  N3: Part1.no_name_yet#connector_DTR0, Part1.no_name_yet#connector_GND1, Part1.no_name_yet#connector_TX0, R2.Pin_1
  N4: Part1.no_name_yet#connector_V3, R1.pin_0
